// Logisim project 2.42completo.circ as structural Verilog: 1 circuit, main circuit main
module main (
  output w,
  output out_2,
  output out_3,
  output out_4,
  output out_5,
  output out_6,
  output x,
  output out_8,
  output out_9,
  output y,
  output z
);

  wire _0_out, _1_out, _2_out, _3_out, _4_out, _5_out, _6_out, _7_out, _8_out, _9_out, and_1_out, and_2_out,
       and_3_out, and_4_out, and_5_out, and_6_out, and_7_out, and_8_out, and_9_out, and_10_out, and_11_out,
       and_12_out, and_13_out, and_14_out, and_15_out, and_16_out, and_17_out, and_18_out, and_19_out,
       and_20_out, and_21_out, and_22_out, and_23_out, and_24_out, and_25_out, and_26_out, and_27_out,
       and_28_out, and_29_out, and_30_out, and_31_out, and_32_out, and_33_out, and_34_out, button_2_out,
       button_out, c1_out, c2_out, c3_out, not_1_out, not_2_out, not_3_out, not_4_out, not_5_out, not_6_out,
       not_7_out, not_8_out, not_9_out, not_10_out, not_11_out, not_12_out, not_13_out, not_14_out,
       not_15_out, not_16_out, not_17_out, not_18_out, not_19_out, not_20_out, not_21_out, not_22_out,
       not_23_out, not_24_out, not_25_out, not_26_out, not_27_out, not_28_out, not_29_out, not_30_out,
       not_31_out, r1_out, r2_out, r3_out, r4_out, xnor_1_out, xnor_2_out, xor_1_out;

  Button _1 (.out(_1_out));
  Button _4 (.out(_4_out));
  Button _7 (.out(_7_out));
  Button button (.out(button_out));
  Button _2 (.out(_2_out));
  Button _5 (.out(_5_out));
  Button _8 (.out(_8_out));
  Button _0 (.out(_0_out));
  Button _3 (.out(_3_out));
  Button _6 (.out(_6_out));
  Button _9 (.out(_9_out));
  Button button_2 (.out(button_2_out));
  or r1 (r1_out, _1_out, _2_out, _3_out);
  or c1 (c1_out, _1_out, _4_out, _7_out, button_out);
  or c2 (c2_out, _2_out, _5_out, _8_out, _0_out);
  or c3 (c3_out, _6_out, _3_out, _9_out, button_2_out);
  or r2 (r2_out, _5_out, _6_out, _4_out);
  or r3 (r3_out, _7_out, _9_out, _8_out);
  or r4 (r4_out, button_out, _0_out, button_2_out);
  not not_1 (not_1_out, r1_out);
  not not_2 (not_2_out, r2_out);
  not not_3 (not_3_out, r3_out);
  not not_4 (not_4_out, r4_out);
  not not_5 (not_5_out, c1_out);
  not not_6 (not_6_out, c2_out);
  not not_7 (not_7_out, c3_out);
  not not_8 (not_8_out, r1_out);
  not not_9 (not_9_out, r2_out);
  not not_10 (not_10_out, r3_out);
  not not_11 (not_11_out, r4_out);
  not not_12 (not_12_out, c1_out);
  not not_13 (not_13_out, c2_out);
  not not_14 (not_14_out, c3_out);
  not not_15 (not_15_out, r1_out);
  not not_16 (not_16_out, r2_out);
  not not_17 (not_17_out, r3_out);
  not not_18 (not_18_out, r4_out);
  not not_19 (not_19_out, c1_out);
  not not_20 (not_20_out, c2_out);
  not not_21 (not_21_out, c3_out);
  not not_22 (not_22_out, r1_out);
  not not_23 (not_23_out, r2_out);
  not not_24 (not_24_out, r3_out);
  not not_25 (not_25_out, r4_out);
  not not_26 (not_26_out, c1_out);
  not not_27 (not_27_out, c2_out);
  not not_28 (not_28_out, c3_out);
  and and_1 (and_1_out, r3_out, c2_out);
  and and_2 (and_2_out, r3_out, c3_out);
  and and_3 (and_3_out, r4_out, c1_out);
  and and_4 (and_4_out, r4_out, c3_out);
  and and_5 (and_5_out, not_1_out, not_2_out, not_3_out, not_4_out, not_5_out, not_6_out, not_7_out);
  and and_6 (and_6_out, r2_out, c1_out);
  and and_7 (and_7_out, r2_out, c2_out);
  and and_8 (and_8_out, r2_out, c3_out);
  and and_9 (and_9_out, r3_out, c1_out);
  and and_10 (and_10_out, not_8_out, not_9_out, not_10_out, not_11_out, not_12_out, not_13_out, not_14_out);
  and and_11 (and_11_out, r1_out, c2_out);
  and and_12 (and_12_out, r1_out, c3_out);
  and and_13 (and_13_out, r2_out, c3_out);
  and and_14 (and_14_out, r3_out, c1_out);
  and and_15 (and_15_out, r4_out, c1_out);
  and and_16 (and_16_out, r4_out, c3_out);
  and and_17 (and_17_out, not_15_out, not_16_out, not_17_out, not_18_out, not_19_out, not_20_out, not_21_out);
  and and_18 (and_18_out, r1_out, c1_out);
  and and_19 (and_19_out, r1_out, c3_out);
  and and_20 (and_20_out, r2_out, c2_out);
  and and_21 (and_21_out, r3_out, c1_out);
  and and_22 (and_22_out, r3_out, c3_out);
  and and_23 (and_23_out, r4_out, c3_out);
  and and_24 (and_24_out, not_22_out, not_23_out, not_24_out, not_25_out, not_26_out, not_27_out, not_28_out);
  or or_1 (w, and_1_out, and_2_out, and_3_out, and_4_out, and_5_out);
  or or_2 (x, and_6_out, and_7_out, and_8_out, and_9_out, and_10_out);
  or or_3 (y, and_11_out, and_12_out, and_13_out, and_14_out, and_15_out, and_16_out, and_17_out);
  or or_4 (z, and_18_out, and_19_out, and_20_out, and_21_out, and_22_out, and_23_out, and_24_out);
  not not_29 (not_29_out, x);
  not not_30 (not_30_out, y);
  not not_31 (not_31_out, z);
  not not_32 (not_31_out, z);
  xnor xnor_1 (xnor_1_out, x, z);
  xnor xnor_2 (xnor_2_out, y, z);
  and and_25 (and_25_out, y, not_31_out);
  and and_26 (and_26_out, not_29_out, y);
  and and_27 (and_27_out, not_29_out, not_31_out);
  and and_28 (and_28_out, x, not_30_out, z);
  and and_29 (and_29_out, y, not_31_out);
  and and_30 (and_30_out, not_29_out, not_31_out);
  and and_31 (and_31_out, not_30_out, not_31_out);
  and and_32 (and_32_out, x, not_31_out);
  and and_33 (and_33_out, x, not_30_out);
  xor xor_1 (xor_1_out, x, y);
  and and_34 (and_34_out, x, not_31_out);
  or a (out_2, w, y, xnor_1_out);
  or b (out_3, not_29_out, xnor_2_out);
  or c (out_4, not_30_out, z, x);
  or d (out_5, and_25_out, and_26_out, and_27_out, and_28_out);
  or e (out_6, and_29_out, and_30_out, and_30_out);
  or f (out_8, and_31_out, and_32_out, w, and_33_out);
  or g (out_9, xor_1_out, w, and_34_out);
  _7_Segment_Display u_7_segment_display_1 (
    .g(out_9), .f(out_8), .a(out_2), .b(out_3), .e(out_6), .d(out_5), .c(out_4));  // open: dp

  // Notes on the sheet:
  //   r2
  //   r3
  //   r1
  //   r4
  //   c1
  //   c2
  //   c3
  //   c
  //   d
  //   e
  //   f
  //   g
  //   a
  //   b
endmodule
